# Fritzing sketch lab_2 (saved by Fritzing 0.8.7b)
breadboards: 1

parts:
  Part1 = Arduino Uno (Rev3)
  R2 = Resistor [tolerance=±5% resistance=560 package=THT]
  LED3 = LED - 5mm [color="Red (633nm)" package="5 mm [THT]"]
  J1 = Piezo Speaker
  R4 = Rotary Potentiometer (Small) [maximum_resistance=100kΩ package=THT]

nets:
  N1: Part1.A0, R4.wiper
  N2: Part1.D4, LED3.cathode
  N3: Part1.D5_PWM, J1.pin1
  N4: Part1.5V, R4.leg1
  N5: Part1.GND, R2.Pin_1, J1.pin2, R4.leg2
  N6: R2.Pin_0, LED3.anode
