# Fritzing sketch lab_4 (saved by Fritzing 0.8.7b)
breadboards: 1

parts:
  Part1 = Arduino Uno (Rev3)
  R2 = Resistor [tolerance=±5% resistance=560 package=THT]
  LED3 = LED - 5mm [color="Red (633nm)" package="5 mm [THT]"]
  S6 = Pushbutton [package="[THT]"]
  R9 = Resistor [tolerance=±5% resistance=560 package=THT]
  LED4 = LED - 5mm [color="Red (633nm)" package="5 mm [THT]"]
  R10 = Resistor [tolerance=±5% resistance=560 package=THT]
  LED5 = LED - 5mm [color="Red (633nm)" package="5 mm [THT]"]
  R11 = Resistor [tolerance=±5% resistance=560 package=THT]

nets:
  N1: Part1.D2, Part1.5V, S6.Pin_3, S6.Pin_4, R9.Pin_0, R9.Pin_1
  N2: Part1.D3_PWM, LED5.cathode
  N3: Part1.D4, LED4.cathode
  N4: Part1.D5_PWM, LED3.cathode
  N5: Part1.GND, R2.Pin_1, R10.Pin_1, R11.Pin_1
  N6: R2.Pin_0, LED3.anode
  N7: S6.Pin_1, S6.Pin_2
  N8: LED4.anode, R10.Pin_0
  N9: LED5.anode, R11.Pin_0
