# Fritzing sketch lab_7 (saved by Fritzing 0.9.2b)
breadboards: 2

parts:
  Part1 = Arduino Uno (Rev3)
  LED5 = RGB LED (com. anode, rbg) [package="5 mm [THT]"]
  R12 = Resistor [tolerance=±5% resistance=560 package=THT]
  R13 = Resistor [tolerance=±5% resistance=560 package=THT]
  U1 = TMP36 [package=to-92-kit]
  DFRobot_LCD_keypad_shield1 = LCD keypad Shield  # not connected

nets:
  N1: Part1.A1, U1.VOUT
  N2: Part1.D9_PWM, R13.Pin_0
  N3: Part1.D10_PWM/SS, R12.Pin_0
  5V: Part1.5V, LED5.common_anode, U1.VCC
  GND: Part1.GND, U1.GND
  N4: LED5.red_cathode, R12.Pin_1
  N5: LED5.blue_cathode, R13.Pin_1

custom parts:
  LCD keypad Shield: A 2 row LCD shield with buttons, and contrast regulator.
